// Logisim project cpu.circ as structural Verilog: 1 circuit, main circuit main
module main (
  input  clock_run,
  input  clock_halt,
  input  in_3,
  input  in_4,
  input  [7:0] data_in,
  input  [15:0] addr_in,
  input  ip_to_addr,
  input  ip_hi_to_data,
  input  ip_lo_to_data,
  input  ip_inc,
  input  data_to_ip_lo,
  input  data_to_ip_hi,
  input  addr_to_ip,
  input  data_to_ir,
  input  mar_hi_to_data,
  input  mar_lo_to_data,
  input  mar_inc,
  input  data_to_mar_lo,
  input  data_to_mar_hi,
  input  addr_to_mar,
  input  data_to_mdr,
  input  mdr_to_data,
  input  data_to_a,
  input  a_to_x,
  input  a_to_data,
  input  data_to_y,
  input  alu_sub,
  input  z_to_data,
  input  alu_to_flags,
  input  data_to_b,
  input  b_to_data,
  input  data_to_c,
  input  c_to_data,
  input  data_to_d,
  input  d_to_data,
  input  data_to_l,
  input  l_to_data,
  input  data_to_h,
  input  h_to_data,
  input  hl_to_addr,
  output clock_halt_2,
  output clock_inv,
  output clock,
  output [7:0] data,
  output [15:0] addr,
  output [15:0] ip,
  output [7:0] ip_lo,
  output [7:0] ip_hi,
  output [7:0] out_49,
  output [15:0] mar,
  output [7:0] mar_lo,
  output [7:0] mar_hi,
  output [7:0] mdr,
  output [7:0] a,
  output [7:0] x,
  output [7:0] y,
  output [7:0] z,
  output [3:0] flags,
  output [7:0] b,
  output [7:0] c,
  output [7:0] d,
  output [7:0] l,
  output [7:0] h,
  output [15:0] hl___m,
  output out_65
);

  wire adder_2_cout, and_1_out, and_2_out, and_3_out, and_4_out, and_5_out, and_6_out, and_8_out, and_9_out,
       clock_1_out, clock_step_out, counter_3_carry, counter_4_carry, counter_5_carry, counter_6_carry,
       counter_7_carry, counter_8_carry, ip_reset_out, nor_1_out, nor_2_out, nor_3_out, nor_4_out, nor_5_out,
       nor_6_out, not_1_out, not_2_out, not_3_out, or_1_out, or_2_out, or_3_out, or_4_out, or_5_out,
       or_6_out, or_7_out, or_8_out, or_9_out, or_10_out, or_11_out;
  wire [1:0] adder_1_cout;
  wire [3:0] bit_extender_1_out, controlled_buffer_5_out, controlled_buffer_9_out, xor_1_out, xor_2_out;
  wire [15:4] controlled_buffer_5_out_2, controlled_buffer_9_out_2;

  assign data = in_3 ? data_in : 8'bz;  // Controlled_Buffer controlled_buffer_1
  assign data = ip_hi_to_data ? ip[15:8] : 8'bz;  // Controlled_Buffer controlled_buffer_2
  assign data = ip_lo_to_data ? ip[7:0] : 8'bz;  // Controlled_Buffer controlled_buffer_3
  Counter #(.width(4), .max('hf)) counter_1 (
    .load(or_3_out), .D(controlled_buffer_5_out_2[15:12]), .count(ip_inc), .Q(ip[15:12]), .clk(or_1_out),
    .clr(ip_reset_out));  // open: carry
  or or_1 (or_1_out, nor_1_out, and_1_out);
  assign controlled_buffer_5_out_2[15:8] = data_to_ip_hi ? data : 8'bz;  // Controlled_Buffer controlled_buffer_4
  assign {controlled_buffer_5_out_2[7:4], controlled_buffer_5_out} = data_to_ip_lo ? data : 8'bz;  // Controlled_Buffer controlled_buffer_5
  assign data = mar_hi_to_data ? mar[15:8] : 8'bz;  // Controlled_Buffer controlled_buffer_6
  assign data = mar_lo_to_data ? mar[7:0] : 8'bz;  // Controlled_Buffer controlled_buffer_7
  Counter #(.width(4), .max('hf)) counter_2 (
    .load(or_5_out), .D(controlled_buffer_9_out_2[15:12]), .count(mar_inc), .Q(mar[15:12]), .clk(or_2_out));  // open: carry, clr
  or or_2 (or_2_out, nor_2_out, and_2_out);
  assign controlled_buffer_9_out_2[15:8] = data_to_mar_hi ? data : 8'bz;  // Controlled_Buffer controlled_buffer_8
  assign {controlled_buffer_9_out_2[7:4], controlled_buffer_9_out} = data_to_mar_lo ? data : 8'bz;  // Controlled_Buffer controlled_buffer_9
  assign mdr = data_to_mdr ? data : 8'bz;  // Controlled_Buffer controlled_buffer_10
  assign data = mdr_to_data ? mdr : 8'bz;  // Controlled_Buffer controlled_buffer_11
  assign data = a_to_data ? a : 8'bz;  // Controlled_Buffer controlled_buffer_12
  assign data = z_to_data ? z : 8'bz;  // Controlled_Buffer controlled_buffer_13
  assign data = b_to_data ? b : 8'bz;  // Controlled_Buffer controlled_buffer_14
  assign data = c_to_data ? c : 8'bz;  // Controlled_Buffer controlled_buffer_15
  assign data = d_to_data ? d : 8'bz;  // Controlled_Buffer controlled_buffer_16
  assign data = l_to_data ? hl___m[7:0] : 8'bz;  // Controlled_Buffer controlled_buffer_17
  assign data = h_to_data ? h : 8'bz;  // Controlled_Buffer controlled_buffer_18
  nor nor_1 (nor_1_out, counter_3_carry, or_3_out);
  nor nor_2 (nor_2_out, counter_4_carry, or_5_out);
  not not_1 (not_1_out, data_to_mdr);
  assign bit_extender_1_out = {{3{alu_sub}}, alu_sub};  // Bit_Extender bit_extender_1
  Button clock_step (.out(clock_step_out));
  and and_1 (and_1_out, or_3_out, clock);
  or or_3 (or_3_out, data_to_ip_hi, addr_to_ip);
  or or_4 (or_4_out, data_to_ip_lo, addr_to_ip);
  and and_2 (and_2_out, or_5_out, clock);
  or or_5 (or_5_out, data_to_mar_hi, addr_to_mar);
  or or_6 (or_6_out, data_to_mar_lo, addr_to_mar);
  Register #(.width(4)) register_1 (.D(data[7:4]), .en(data_to_a), .Q(a[7:4]), .clk(clock));  // open: clr
  Register #(.width(4)) register_2 (.D(data[7:4]), .en(data_to_y), .Q(y[7:4]), .clk(clock));  // open: clr
  Register #(.width(4)) register_3 (.D(data[7:4]), .en(data_to_b), .Q(b[7:4]), .clk(clock));  // open: clr
  Register #(.width(4)) register_4 (.D(data[7:4]), .en(data_to_c), .Q(c[7:4]), .clk(clock));  // open: clr
  Register #(.width(4)) register_5 (.D(data[7:4]), .en(data_to_d), .Q(d[7:4]), .clk(clock));  // open: clr
  Register #(.width(4)) register_6 (.D(data[7:4]), .en(data_to_l), .Q(hl___m[7:4]), .clk(clock));  // open: clr
  Register #(.width(4)) register_7 (.D(data[7:4]), .en(data_to_h), .Q(h[7:4]), .clk(clock));  // open: clr
  Clock clock_1 (.out(clock_1_out));
  not not_2 (not_2_out, clock_run);
  Counter #(.width(4), .max('hf)) counter_3 (
    .load(or_3_out), .D(controlled_buffer_5_out_2[11:8]), .count(ip_inc), .Q(ip[11:8]),
    .carry(counter_3_carry), .clk(or_7_out), .clr(ip_reset_out));
  Register register_8 (.D(data), .en(data_to_ir), .Q(out_49), .clk(clock));  // open: clr
  Counter #(.width(4), .max('hf)) counter_4 (
    .load(or_5_out), .D(controlled_buffer_9_out_2[11:8]), .count(mar_inc), .Q(mar[11:8]),
    .carry(counter_4_carry), .clk(or_8_out));  // open: clr
  Register #(.width(4)) register_9 (.D(data[3:0]), .en(data_to_a), .Q(a[3:0]), .clk(clock));  // open: clr
  Register #(.width(4)) register_10 (.D(data[3:0]), .en(data_to_y), .Q(y[3:0]), .clk(clock));  // open: clr
  assign xor_1_out = y[7:4] ^ bit_extender_1_out;  // XOR_Gate xor_1, 4 bits wide
  Register #(.width(4)) register_11 (.D(data[3:0]), .en(data_to_b), .Q(b[3:0]), .clk(clock));  // open: clr
  Register #(.width(4)) register_12 (.D(data[3:0]), .en(data_to_c), .Q(c[3:0]), .clk(clock));  // open: clr
  Register #(.width(4)) register_13 (.D(data[3:0]), .en(data_to_d), .Q(d[3:0]), .clk(clock));  // open: clr
  Register #(.width(4)) register_14 (.D(data[3:0]), .en(data_to_l), .Q(hl___m[3:0]), .clk(clock));  // open: clr
  Register #(.width(4)) register_15 (.D(data[3:0]), .en(data_to_h), .Q(h[3:0]), .clk(clock));  // open: clr
  and and_3 (and_3_out, clock_1_out, clock_run);
  and and_4 (and_4_out, not_2_out, clock_step_out);
  not not_3 (not_3_out, clock_halt);
  or or_7 (or_7_out, nor_3_out, and_5_out);
  or or_8 (or_8_out, nor_4_out, and_6_out);
  or or_9 (or_9_out, and_3_out, and_4_out);
  nor nor_3 (nor_3_out, counter_5_carry, or_3_out);
  and and_5 (and_5_out, or_3_out, clock);
  nor nor_4 (nor_4_out, counter_6_carry, or_5_out);
  and and_6 (and_6_out, or_5_out, clock);
  assign xor_2_out = y[3:0] ^ bit_extender_1_out;  // XOR_Gate xor_2, 4 bits wide
  and and_7 (clock, or_9_out, not_3_out);
  Adder #(.width(4)) adder_1 (.a(x[7:4]), .b(xor_1_out), .out(z[7:4]), .cin(adder_2_cout), .cout(adder_1_cout[0]));
  Register #(.width(4)) register_16 (
    .D({2'b00, adder_1_cout}), .en(alu_to_flags), .Q(flags), .clk(clock));  // open: clr
  not not_4 (clock_inv, clock);
  Counter #(.width(4), .max('hf)) counter_5 (
    .load(or_4_out), .D(controlled_buffer_5_out_2[7:4]), .count(ip_inc), .Q(ip[7:4]),
    .carry(counter_5_carry), .clk(or_10_out), .clr(ip_reset_out));
  or or_10 (or_10_out, nor_5_out, and_8_out);
  Counter #(.width(4), .max('hf)) counter_6 (
    .load(or_6_out), .D(controlled_buffer_9_out_2[7:4]), .count(mar_inc), .Q(mar[7:4]),
    .carry(counter_6_carry), .clk(or_11_out));  // open: clr
  or or_11 (or_11_out, nor_6_out, and_9_out);
  Register #(.width(4)) register_17 (.D(a[7:4]), .en(a_to_x), .Q(x[7:4]), .clk(clock));  // open: clr
  Adder #(.width(4)) adder_2 (.a(x[3:0]), .b(xor_2_out), .out(z[3:0]), .cin(alu_sub), .cout(adder_2_cout));
  nor nor_5 (nor_5_out, counter_7_carry, or_4_out);
  and and_8 (and_8_out, or_4_out, clock);
  nor nor_6 (nor_6_out, counter_8_carry, or_6_out);
  and and_9 (and_9_out, or_6_out, clock);
  RAM #(.addrWidth(16)) ram_1 (.addr(mar), .data(mdr), .sel(1'b1), .clk(clock), .ld(not_1_out));  // open: clr
  Register #(.width(4)) register_18 (.D(a[3:0]), .en(a_to_x), .Q(x[3:0]), .clk(clock));  // open: clr
  Counter #(.width(4), .max('hf)) counter_7 (
    .load(or_4_out), .D(controlled_buffer_5_out), .count(ip_inc), .Q(ip[3:0]), .carry(counter_7_carry),
    .clk(clock), .clr(ip_reset_out));
  Counter #(.width(4), .max('hf)) counter_8 (
    .load(or_6_out), .D(controlled_buffer_9_out), .count(mar_inc), .Q(mar[3:0]), .carry(counter_8_carry),
    .clk(clock));  // open: clr
  assign addr = in_4 ? addr_in : 16'bz;  // Controlled_Buffer controlled_buffer_19
  assign addr = ip_to_addr ? ip : 16'bz;  // Controlled_Buffer controlled_buffer_20
  assign {controlled_buffer_5_out_2, controlled_buffer_5_out} = addr_to_ip ? addr : 16'bz;  // Controlled_Buffer controlled_buffer_21
  assign {controlled_buffer_9_out_2, controlled_buffer_9_out} = addr_to_mar ? addr : 16'bz;  // Controlled_Buffer controlled_buffer_22
  assign addr = hl_to_addr ? {h, hl___m[7:0]} : 16'bz;  // Controlled_Buffer controlled_buffer_23
  Button ip_reset (.out(ip_reset_out));

  assign clock_halt_2 = clock_halt;
  assign hl___m[15:8] = h;
  assign ip_hi = ip[15:8];
  assign ip_lo = ip[7:0];
  assign l = hl___m[7:0];
  assign mar_hi = mar[15:8];
  assign mar_lo = mar[7:0];

  // Notes on the sheet:
  //   8-Bit Data Bus
  //   Memory Data Register
  //   A Register
  //   Y Register
  //   B Register
  //   C Register
  //   D Register
  //   L Register
  //   H Register
  //   Clock
  //   Instruction Register
  //   ZC
  //   Memory Address Register
  //   HL Registers / M
  //   16-Bit Address Bus
  //   Instruction Pointer
  //   Arithmetic Logic Unit
  //   Flags Register
  //   X Register
  //   Z Register
endmodule
